// Logisim project BancoRegistradores.circ as structural Verilog
module BancoRegistradores (
  input  [7:0] Entrada,
  input  nZero,
  input  ClcGen,
  input  In_Out,
  input  [1:0] WrAddr,
  output [7:0] Saida
);

  wire Clk_out, decoder_1_out0, decoder_1_out1, decoder_1_out2, decoder_1_out3, not_1_out;
  wire [7:0] controlled_inverter_1_out, register_1_q, register_2_q, register_3_q, register_4_q;

  // Probe on Entrada
  Clock Clk (.out(Clk_out));
  // Probe on controlled_inverter_1_out
  assign controlled_inverter_1_out = nZero ? ~Entrada : 8'bz;  // Controlled_Inverter controlled_inverter_1
  Pull_Resistor pull_resistor_1 (.node(controlled_inverter_1_out));
  Decoder #(.select(2), .disabled(0)) decoder_1 (
    .out0(decoder_1_out0), .out1(decoder_1_out1), .out2(decoder_1_out2), .out3(decoder_1_out3), .sel(WrAddr),
    .en(not_1_out));
  not not_1 (not_1_out, In_Out);
  Register register_1 (
    .D(controlled_inverter_1_out), .en(decoder_1_out0), .Q(register_1_q), .clk(Clk_out), .clr(ClcGen));
  Register register_2 (
    .D(controlled_inverter_1_out), .en(decoder_1_out1), .Q(register_2_q), .clk(Clk_out), .clr(ClcGen));
  Register register_3 (
    .D(controlled_inverter_1_out), .en(decoder_1_out2), .Q(register_3_q), .clk(Clk_out), .clr(ClcGen));
  Register register_4 (
    .D(controlled_inverter_1_out), .en(decoder_1_out3), .Q(register_4_q), .clk(Clk_out), .clr(ClcGen));
  Multiplexer #(.select(2), .width(8)) multiplexer_1 (
    .in0(register_1_q), .in1(register_2_q), .in2(register_3_q), .in3(register_4_q), .out(Saida),
    .sel(WrAddr), .en(In_Out));

  // Notes on the sheet:
  //   Sistema SISO
  //   Single Input Single Output
endmodule

module BancoRegistradosRealimentacao (
  input  [7:0] Entrada,
  input  En,
  input  Clr,
  input  [1:0] In,
  input  [1:0] Out,
  output [7:0] Saida
);

  wire Clk_out;
  wire [7:0] demultiplexer_1_out0, demultiplexer_1_out1, demultiplexer_1_out2, demultiplexer_1_out3, R1_q,
       R2_q, R3_q, R4_q;

  Clock Clk (.out(Clk_out));
  Demultiplexer #(.select(2), .width(8)) demultiplexer_1 (
    .out0(demultiplexer_1_out0), .out1(demultiplexer_1_out1), .out2(demultiplexer_1_out2),
    .out3(demultiplexer_1_out3), .in(Entrada), .sel(In), .en(En));
  Register R1 (.D(demultiplexer_1_out0), .en(En), .Q(R1_q), .clk(Clk_out), .clr(Clr));
  Register R2 (.D(demultiplexer_1_out1), .en(En), .Q(R2_q), .clk(Clk_out), .clr(Clr));
  Register R3 (.D(demultiplexer_1_out2), .en(En), .Q(R3_q), .clk(Clk_out));  // open: clr
  Register R4 (.D(demultiplexer_1_out3), .en(En), .Q(R4_q), .clk(Clk_out), .clr(Clr));
  assign demultiplexer_1_out0 = R1_q;  // Buffer R1_2, 8 bits wide
  assign demultiplexer_1_out1 = R2_q;  // Buffer R2_2, 8 bits wide
  assign demultiplexer_1_out2 = R3_q;  // Buffer R3_2, 8 bits wide
  assign demultiplexer_1_out3 = R4_q;  // Buffer R4_2, 8 bits wide
  Multiplexer #(.select(2), .width(8)) multiplexer_1 (
    .in0(R1_q), .in1(R2_q), .in2(R3_q), .in3(R4_q), .out(Saida), .sel(Out), .en(En));
endmodule

module BancoRegistradoresRealimentacaoParaMuitos (
  input  [7:0] Entrada,
  input  [7:0] Entrada2,
  input  [7:0] Entrada3,
  input  [7:0] Entrada4,
  input  [2:0] SlcA,
  input  [2:0] SlcB,
  input  [2:0] SlcC,
  input  [2:0] SlcD,
  input  in_9,
  input  En,
  input  [1:0] Slct,
  input  in_12,
  input  in_13,
  input  in_14,
  input  in_15,
  input  En_2,
  input  [1:0] Slct_2,
  input  in_18,
  input  in_19,
  input  in_20,
  input  in_21,
  input  in_22,
  input  in_23,
  input  in_24,
  output [7:0] Saida,
  output [7:0] Saida2
);

  wire Clk;
  wire [7:0] multiplexer_1_out, multiplexer_2_out, multiplexer_3_out, multiplexer_4_out, SR1, SR2, SR3, SR4;

  Clock u_Clk (.out(Clk));
  Multiplexer #(.select(3), .width(8)) multiplexer_1 (
    .in0(Entrada), .in1(SR1), .in2(SR2), .in3(SR3), .in4(SR4), .in5(Entrada2), .in6(Entrada3),
    .in7(Entrada4), .out(multiplexer_1_out), .sel(SlcA), .en(in_9));
  Multiplexer #(.select(3), .width(8)) multiplexer_2 (
    .in0(Entrada), .in1(SR1), .in2(SR2), .in3(SR3), .in4(SR4), .in5(Entrada2), .in6(Entrada3),
    .in7(Entrada4), .out(multiplexer_2_out), .sel(SlcB), .en(in_12));
  Multiplexer #(.select(3), .width(8)) multiplexer_3 (
    .in0(Entrada), .in1(SR1), .in2(SR2), .in3(SR3), .in4(SR4), .in5(Entrada2), .in6(Entrada3),
    .in7(Entrada4), .out(multiplexer_3_out), .sel(SlcC), .en(in_13));
  Multiplexer #(.select(3), .width(8)) multiplexer_4 (
    .in0(Entrada), .in1(SR1), .in2(SR2), .in3(SR3), .in4(SR4), .in5(Entrada2), .in6(Entrada3),
    .in7(Entrada4), .out(multiplexer_4_out), .sel(SlcD), .en(in_14));
  Register R1 (.D(multiplexer_1_out), .en(in_15), .Q(SR1), .clk(Clk), .clr(in_21));
  Register R2 (.D(multiplexer_2_out), .en(in_18), .Q(SR2), .clk(Clk), .clr(in_22));
  Register R3 (.D(multiplexer_3_out), .en(in_19), .Q(SR3), .clk(Clk), .clr(in_23));
  Register R4 (.D(multiplexer_4_out), .en(in_20), .Q(SR4), .clk(Clk), .clr(in_24));
  Multiplexer #(.select(2), .width(8)) multiplexer_5 (
    .in0(SR1), .in1(SR2), .in2(SR3), .in3(SR4), .out(Saida), .sel(Slct), .en(En));
  Multiplexer #(.select(2), .width(8)) multiplexer_6 (
    .in0(SR1), .in1(SR2), .in2(SR3), .in3(SR4), .out(Saida2), .sel(Slct_2), .en(En_2));

  // Other names for the same wires on the sheet: ClcR1 = in_21; ClcR2 = in_22; ClcR3 = in_23; ClcR4 = in_24;
  //   EnA = in_9; EnB = in_12; EnC = in_13; EnD = in_14; EnR1 = in_15; EnR2 = in_18; EnR3 = in_19; EnR4 = in_20
endmodule

module RegistradorDeInstrucoes (
  input  [7:0] in_1,
  input  in_2,
  input  in_3,
  output [7:0] Saida
);

  wire clock_1_out, controlled_buffer_1_out, controlled_buffer_3_out, controlled_buffer_4_out, decoder_1_out0;
  wire [1:0] controlled_buffer_2_out;
  wire [7:0] register_1_q, undriven;

  Register register_1 (.D(in_1), .en(in_2), .Q(register_1_q), .clk(clock_1_out), .clr(in_3));
  Clock clock_1 (.out(clock_1_out));
  Decoder #(.select(2), .disabled(0)) decoder_1 (
    .out0(decoder_1_out0), .sel(register_1_q[7:6]));  // open: out1, out2, out3, en
  assign controlled_buffer_1_out = decoder_1_out0 ? register_1_q[2] : 1'bz;  // Controlled_Buffer controlled_buffer_1
  assign controlled_buffer_2_out = decoder_1_out0 ? register_1_q[1:0] : 2'bz;  // Controlled_Buffer controlled_buffer_2
  assign controlled_buffer_3_out = decoder_1_out0 ? register_1_q[4] : 1'bz;  // Controlled_Buffer controlled_buffer_3
  assign controlled_buffer_4_out = decoder_1_out0 ? register_1_q[3] : 1'bz;  // Controlled_Buffer controlled_buffer_4
  BancoRegistradores bancoregistradores_1 (
    .Entrada(undriven), .nZero(controlled_buffer_4_out), .ClcGen(controlled_buffer_3_out),
    .In_Out(controlled_buffer_1_out), .WrAddr(controlled_buffer_2_out), .Saida(Saida));
endmodule
