// Logisim project Memoria.circ as structural Verilog
module Memoria (
  input  in_1,
  input  in_2,
  input  [2:0] in_3,
  input  in_4,
  input  in_5,
  input  ClrCount,
  input  [7:0] in_7,
  input  CS__Chip_Select,
  input  Load,
  input  ClrMem,
  output [7:0] out_11
);

  wire Clock_out;
  wire [2:0] counter_1_q;
  wire [7:0] ram_1_data;

  Clock Clock (.out(Clock_out));
  // Probe on in_3
  Counter #(.width(3), .max('h7)) counter_1 (
    .load(in_1), .D(in_3), .count(in_5), .Q(counter_1_q), .clk(Clock_out), .clr(ClrCount));  // open: carry
  RAM #(.addrWidth(3)) ram_1 (
    .addr(counter_1_q), .data(ram_1_data), .sel(CS__Chip_Select), .clk(Clock_out), .ld(Load), .clr(ClrMem));
  assign ram_1_data = in_4 ? in_7 : 8'bz;  // Controlled_Buffer controlled_buffer_1
  // Probe on out_11
  assign out_11 = in_2 ? ram_1_data : 8'bz;  // Controlled_Buffer controlled_buffer_2
  // Probe on in_7

  // Notes on the sheet:
  //   Armazene ff8842
endmodule
