// Logisim project SomadorConversor8para16.circ as structural Verilog
module Somador (
  input  in_1,
  input  [7:0] A,
  input  [7:0] B,
  output [7:0] out_4,
  output out_5
);

  // Probe on A
  // Probe on B
  // Probe on A
  // Probe on B
  // Probe on A
  // Probe on B
  // Probe on out_4
  Adder adder_1 (.a(A), .b(B), .out(out_4), .cin(in_1), .cout(out_5));
  // Probe on out_4
  // Probe on {out_5, out_4}
  // Probe on out_4
endmodule

module _8para16 (
  input  [7:0] In8,
  input  Sign,
  output [15:0] Out16
);

  and and_1 (Out16[15], In8[7], Sign);

  assign Out16[14:0] = {{7{Out16[15]}}, In8};
endmodule

module _8para32 (
  input  [7:0] In8,
  input  in_2,
  output [31:0] Out16
);

  and and_1 (Out16[31], In8[7], in_2);

  assign Out16[30:0] = {{23{Out16[31]}}, In8};
endmodule

module _16para32 (
  input  [15:0] In8,
  input  in_2,
  output [31:0] Out16
);

  and and_1 (Out16[31], In8[15], in_2);

  assign Out16[30:0] = {{15{Out16[31]}}, In8};
endmodule

module MemoriaRam (
  input  in_1,
  input  in_2,
  input  [2:0] in_3,
  input  in_4,
  input  ClrCount,
  input  in_6,
  input  CS__Chip_Select,
  input  [7:0] in_8,
  input  Load,
  input  ClrMem,
  output [7:0] out_11,
  output [15:0] out_12
);

  wire Clock_out;
  wire [2:0] counter_1_q;
  wire [7:0] ram_1_data;

  Clock Clock (.out(Clock_out));
  // Probe on in_3
  Counter #(.width(3), .max('h7)) counter_1 (
    .load(in_1), .D(in_3), .count(in_4), .Q(counter_1_q), .clk(Clock_out), .clr(ClrCount));  // open: carry
  RAM #(.addrWidth(3)) ram_1 (
    .addr(counter_1_q), .data(ram_1_data), .sel(CS__Chip_Select), .clk(Clock_out), .ld(Load), .clr(ClrMem));
  assign ram_1_data = in_6 ? in_8 : 8'bz;  // Controlled_Buffer controlled_buffer_1
  // Probe on out_11
  assign out_11 = in_2 ? ram_1_data : 8'bz;  // Controlled_Buffer controlled_buffer_2
  // Probe on in_8
  // Probe on out_12
  _8para16 u_8para16_1 (.In8(out_11), .Out16(out_12));  // open: Sign

  // Notes on the sheet:
  //   Armazene ff8842
endmodule

module _16para8 (
  input  [15:0] in_1,
  output [7:0] out_2
);

  wire clock_1_out, not_1_out;

  Clock clock_1 (.out(clock_1_out));
  not not_1 (not_1_out, clock_1_out);
  assign out_2 = not_1_out ? in_1[7:0] : 8'bz;  // Controlled_Buffer controlled_buffer_1
  assign out_2 = clock_1_out ? in_1[15:8] : 8'bz;  // Controlled_Buffer controlled_buffer_2
endmodule
